// Logisim project TicTacToe.circ as structural Verilog: 35 circuits, main circuit CdM-8
module main (
);

  wire and_3_out, button_2_out, button_3_out, button_4_out, button_5_out, button_6_out, button_7_out,
       button_8_out, button_9_out, button_10_out, cdm_8_1_data_code_prime, Cl, code, comparator_1_eq,
       comparator_2_eq, data, decoder_2_out0, decoder_2_out1, gsdd_1_draw, gsdd_1_lose, gsdd_1_win, I_Osel,
       In_out_prime, IO_3_2_out, IO_3_out, mem, not_1_out, or_1_out, RAM, rst;
  wire [1:0] _1, _2, _3, _4, _5, _6, _7, _8, _9, sdr_1_h0, sdr_1_h1, sdr_1_h2, sdr_1_v0, sdr_1_v1, sdr_1_v2;
  wire [2:2] tttc_1_hout, tttc_1_vout, tttc_2_vout, tttc_3_vout, tttc_4_hout, tttc_7_hout;
  wire [3:0] I_Oadr, tttc_1_l0, tttc_1_l1, tttc_1_l2, tttc_1_l3, tttc_2_l0, tttc_2_l1, tttc_2_l2, tttc_2_l3,
       tttc_3_l0, tttc_3_l1, tttc_3_l2, tttc_3_l3, tttc_4_l0, tttc_4_l1, tttc_4_l2, tttc_4_l3, tttc_5_l0,
       tttc_5_l1, tttc_5_l2, tttc_5_l3, tttc_6_l0, tttc_6_l1, tttc_6_l2, tttc_6_l3, tttc_7_l0, tttc_7_l1,
       tttc_7_l2, tttc_7_l3, tttc_8_l0, tttc_8_l1, tttc_8_l2, tttc_8_l3, tttc_9_l0, tttc_9_l1, tttc_9_l2,
       tttc_9_l3;
  wire [7:0] bpc_1_xy, cdm_8_1_data_out, cdm_8_1_pc, cdm_8_1_ps, cdm_8_1_r0, cdm_8_1_r1, cdm_8_1_r2,
       cdm_8_1_r3, cdm_8_1_sp, computer_turn_1_coords, controlled_buffer_2_out, I_Odat;
  wire [7:4] cdm_8_1_addr;

  Clock clock_1 (.out(Cl));
  // Probe on cdm_8_1_r0
  // Probe on cdm_8_1_r1
  Button button_1 (.out(rst));
  and and_1 (I_Osel, or_1_out, Cl, data);
  // Probe on cdm_8_1_pc
  // Probe on cdm_8_1_r2
  // Probe on cdm_8_1_r3
  // Probe on I_Odat
  LED led_1 (.in(gsdd_1_win));
  LED led_2 (.in(gsdd_1_draw));
  LED led_3 (.in(gsdd_1_lose));
  GSDD gsdd_1 (
    .score(I_Odat[7:6]), .clock(decoder_2_out0), .win(gsdd_1_win), .lose(gsdd_1_lose), .draw(gsdd_1_draw),
    .reset(rst));
  // Probe on cdm_8_1_sp
  // Probe on cdm_8_1_ps
  and and_2 (RAM, ~or_1_out, data);  // AND_Gate
  SDR sdr_1 (
    .XY(I_Odat[5:2]), .ID_symbol(I_Odat[1:0]), .H0(sdr_1_h0), .H1(sdr_1_h1), .H2(sdr_1_h2),
    .clock(decoder_2_out0), .V0(sdr_1_v0), .V1(sdr_1_v1), .V2(sdr_1_v2));
  and IO_3 (IO_3_out, I_Osel, I_Oadr[0], I_Oadr[1], I_Oadr[2], ~I_Oadr[3]);  // AND_Gate
  // Probe on {cdm_8_1_addr, I_Oadr}
  CdM_8 cdm_8_1 (
    .data_code_prime(cdm_8_1_data_code_prime), .R0(cdm_8_1_r0), .R1(cdm_8_1_r1), .mem(mem), .R2(cdm_8_1_r2),
    .load_st_prime(In_out_prime), .R3(cdm_8_1_r3), .addr({cdm_8_1_addr, I_Oadr}), .PC(cdm_8_1_pc),
    .SP(cdm_8_1_sp), .data_out(cdm_8_1_data_out), .data_in(controlled_buffer_2_out), .PS(cdm_8_1_ps),
    .clk(Cl), .rset(rst));  // open: page, IAck, IRQ, vector, shadow
  Comparator comparator_1 (.a(8'h7), .b({cdm_8_1_addr, I_Oadr}), .eq(comparator_1_eq));  // open: gt, lt
  Comparator comparator_2 (.a(8'h3), .b({cdm_8_1_addr, I_Oadr}), .eq(comparator_2_eq));  // open: gt, lt
  and IO_3_2 (IO_3_2_out, I_Osel, I_Oadr[0], I_Oadr[1], ~I_Oadr[2], ~I_Oadr[3]);  // AND_Gate
  and and_3 (and_3_out, In_out_prime, IO_3_out);
  computer_turn computer_turn_1 (
    ._1(_1), ._2(_2), ._3(_3), ._4(_4), ._5(_5), ._6(_6), ._7(_7), ._8(_8), ._9(_9),
    .coords(computer_turn_1_coords));
  Decoder #(.disabled(0)) decoder_1 (.out0(code), .out1(data), .sel(cdm_8_1_data_code_prime), .en(mem));
  assign I_Odat = not_1_out ? cdm_8_1_data_out : 8'bz;  // Controlled_Buffer controlled_buffer_1
  not not_1 (not_1_out, In_out_prime);
  assign controlled_buffer_2_out = In_out_prime ? I_Odat : 8'bz;  // Controlled_Buffer controlled_buffer_2
  or or_1 (or_1_out, comparator_2_eq, comparator_1_eq);
  Decoder #(.disabled(0)) decoder_2 (.out0(decoder_2_out0), .out1(decoder_2_out1), .sel(In_out_prime), .en(IO_3_2_out));
  TTTC tttc_1 (
    .hin(sdr_1_v2), .hout(tttc_1_hout[2]), .L0(tttc_1_l0), .L1(tttc_1_l1), .L2(tttc_1_l2), .L3(tttc_1_l3),
    .btn(button_2_out), .vin(sdr_1_h0), .vout(tttc_1_vout[2]), .reset(rst), .state(_1));
  DotMatrix #(.inputtype("row"), .matrixcols(4), .matrixrows(4)) dotmatrix_1 (
    .row0(tttc_1_l0), .row1(tttc_1_l1), .row2(tttc_1_l2), .row3(tttc_1_l3));
  Button button_2 (.out(button_2_out));
  TTTC tttc_2 (
    .hin(sdr_1_v2), .hout(tttc_1_hout[2]), .L0(tttc_2_l0), .L1(tttc_2_l1), .L2(tttc_2_l2), .L3(tttc_2_l3),
    .btn(button_3_out), .vin(sdr_1_h1), .vout(tttc_2_vout[2]), .reset(rst), .state(_2));
  DotMatrix #(.inputtype("row"), .matrixcols(4), .matrixrows(4)) dotmatrix_2 (
    .row0(tttc_2_l0), .row1(tttc_2_l1), .row2(tttc_2_l2), .row3(tttc_2_l3));
  Button button_3 (.out(button_3_out));
  DotMatrix #(.inputtype("row"), .matrixcols(4), .matrixrows(4)) dotmatrix_3 (
    .row0(tttc_3_l0), .row1(tttc_3_l1), .row2(tttc_3_l2), .row3(tttc_3_l3));
  TTTC tttc_3 (
    .hin(sdr_1_v2), .hout(tttc_1_hout[2]), .L0(tttc_3_l0), .L1(tttc_3_l1), .L2(tttc_3_l2), .L3(tttc_3_l3),
    .btn(button_4_out), .vin(sdr_1_h2), .vout(tttc_3_vout[2]), .reset(rst), .state(_3));
  Button button_4 (.out(button_4_out));
  assign I_Odat = and_3_out ? computer_turn_1_coords : 8'bz;  // Controlled_Buffer controlled_buffer_3
  // Probe on computer_turn_1_coords
  Pull_Resistor pull_resistor_1 (.node(I_Oadr[0]));
  Pull_Resistor pull_resistor_2 (.node(I_Oadr[1]));
  Pull_Resistor pull_resistor_3 (.node(I_Oadr[2]));
  Pull_Resistor pull_resistor_4 (.node(I_Oadr[3]));
  Pull_Resistor pull_resistor_5 (.node(cdm_8_1_addr[4]));
  Pull_Resistor pull_resistor_6 (.node(cdm_8_1_addr[5]));
  Pull_Resistor pull_resistor_7 (.node(cdm_8_1_addr[6]));
  Pull_Resistor pull_resistor_8 (.node(cdm_8_1_addr[7]));
  DotMatrix #(.inputtype("row"), .matrixcols(4), .matrixrows(4)) dotmatrix_4 (
    .row0(tttc_4_l0), .row1(tttc_4_l1), .row2(tttc_4_l2), .row3(tttc_4_l3));
  TTTC tttc_4 (
    .hin(sdr_1_v1), .hout(tttc_4_hout[2]), .L0(tttc_4_l0), .L1(tttc_4_l1), .L2(tttc_4_l2), .L3(tttc_4_l3),
    .btn(button_5_out), .vin(sdr_1_h0), .vout(tttc_1_vout[2]), .reset(rst), .state(_4));
  Button button_5 (.out(button_5_out));
  DotMatrix #(.inputtype("row"), .matrixcols(4), .matrixrows(4)) dotmatrix_5 (
    .row0(tttc_5_l0), .row1(tttc_5_l1), .row2(tttc_5_l2), .row3(tttc_5_l3));
  TTTC tttc_5 (
    .hin(sdr_1_v1), .hout(tttc_4_hout[2]), .L0(tttc_5_l0), .L1(tttc_5_l1), .L2(tttc_5_l2), .L3(tttc_5_l3),
    .btn(button_6_out), .vin(sdr_1_h1), .vout(tttc_2_vout[2]), .reset(rst), .state(_5));
  Button button_6 (.out(button_6_out));
  DotMatrix #(.inputtype("row"), .matrixcols(4), .matrixrows(4)) dotmatrix_6 (
    .row0(tttc_6_l0), .row1(tttc_6_l1), .row2(tttc_6_l2), .row3(tttc_6_l3));
  TTTC tttc_6 (
    .hin(sdr_1_v1), .hout(tttc_4_hout[2]), .L0(tttc_6_l0), .L1(tttc_6_l1), .L2(tttc_6_l2), .L3(tttc_6_l3),
    .btn(button_7_out), .vin(sdr_1_h2), .vout(tttc_3_vout[2]), .reset(rst), .state(_6));
  Button button_7 (.out(button_7_out));
  ROM rom_1 (.addr({cdm_8_1_addr, I_Oadr}), .data(I_Odat), .sel(code));
  RAM ram_1 (.addr({cdm_8_1_addr, I_Oadr}), .data(I_Odat), .sel(RAM), .clk(Cl), .ld(In_out_prime), .clr(rst));
  DotMatrix #(.inputtype("row"), .matrixcols(4), .matrixrows(4)) dotmatrix_7 (
    .row0(tttc_7_l0), .row1(tttc_7_l1), .row2(tttc_7_l2), .row3(tttc_7_l3));
  TTTC tttc_7 (
    .hin(sdr_1_v0), .hout(tttc_7_hout[2]), .L0(tttc_7_l0), .L1(tttc_7_l1), .L2(tttc_7_l2), .L3(tttc_7_l3),
    .btn(button_8_out), .vin(sdr_1_h0), .vout(tttc_1_vout[2]), .reset(rst), .state(_7));
  Button button_8 (.out(button_8_out));
  TTTC tttc_8 (
    .hin(sdr_1_v0), .hout(tttc_7_hout[2]), .L0(tttc_8_l0), .L1(tttc_8_l1), .L2(tttc_8_l2), .L3(tttc_8_l3),
    .btn(button_9_out), .vin(sdr_1_h1), .vout(tttc_2_vout[2]), .reset(rst), .state(_8));
  DotMatrix #(.inputtype("row"), .matrixcols(4), .matrixrows(4)) dotmatrix_8 (
    .row0(tttc_8_l0), .row1(tttc_8_l1), .row2(tttc_8_l2), .row3(tttc_8_l3));
  Button button_9 (.out(button_9_out));
  TTTC tttc_9 (
    .hin(sdr_1_v0), .hout(tttc_7_hout[2]), .L0(tttc_9_l0), .L1(tttc_9_l1), .L2(tttc_9_l2), .L3(tttc_9_l3),
    .btn(button_10_out), .vin(sdr_1_h2), .vout(tttc_3_vout[2]), .reset(rst), .state(_9));
  DotMatrix #(.inputtype("row"), .matrixcols(4), .matrixrows(4)) dotmatrix_9 (
    .row0(tttc_9_l0), .row1(tttc_9_l1), .row2(tttc_9_l2), .row3(tttc_9_l3));
  Button button_10 (.out(button_10_out));
  assign I_Odat = decoder_2_out1 ? {bpc_1_xy[7], 1'b0, bpc_1_xy[5:0]} : 8'bz;  // Controlled_Buffer controlled_buffer_4
  BPC bpc_1 (
    .H0(tttc_1_vout[2]), .H1(tttc_2_vout[2]), .H2(tttc_3_vout[2]), .V0(tttc_1_hout[2]), .V1(tttc_4_hout[2]),
    .V2(tttc_7_hout[2]), .reset(decoder_2_out1), .XY(bpc_1_xy[3:0]), .ready(bpc_1_xy[7]));
  check_all check_all_1 (
    ._0_0(_1), ._0_1(_2), ._0_2(_3), ._1_0(_4), ._1_1(_5), ._1_2(_6), ._2_0(_7), ._2_1(_8), ._2_2(_9),
    .out_10(bpc_1_xy[5:4]));

  // Other names for the same wires on the sheet: rd_wr_prime = In_out_prime

  // Notes on the sheet:
  //   contents of rom_1 (hex, n*v repeats v):
  //   d2 3 b9 5 e5 9 b9 ee 3 b4 0 e0 f ee 0 d0 2 a4 75 95 95 11 a9 d6 3f 0 e1 2d d6 37 d1 1 a1 70 94 94 11
  //   a9 d6 3f 0 e1 2d ee 0 d1 3 90 90 90 d2 3c 58 a4 d4 c1 c2 c3 d1 7 b4 ee 4c c1 c2 c3 d1 3 b4 4*98 44
  //   ee 4c c7 c6 c5 d7
endmodule

// LLL
module SDR (
  input  clock,
  input  [3:0] XY,
  input  [1:0] ID_symbol,
  output [1:0] H0,
  output [1:0] H1,
  output [1:0] H2,
  output [1:0] V0,
  output [1:0] V1,
  output [1:0] V2
);

  wire decoder_1_out0, decoder_1_out1, decoder_1_out2, decoder_2_out0, decoder_2_out1, decoder_2_out2,
       undriven, undriven_2;

  Pull_Resistor #(.pull(1)) pull_resistor_1 (.node(XY));
  Decoder #(.select(2)) decoder_1 (
    .out0(decoder_1_out0), .out1(decoder_1_out1), .out2(decoder_1_out2), .sel(XY[3:2]), .en(undriven));  // open: out3
  assign V0 = decoder_1_out2 ? {clock, ID_symbol[1]} : 2'bz;  // Controlled_Buffer controlled_buffer_1
  assign V1 = decoder_1_out1 ? {clock, ID_symbol[1]} : 2'bz;  // Controlled_Buffer controlled_buffer_2
  assign V2 = decoder_1_out0 ? {clock, ID_symbol[1]} : 2'bz;  // Controlled_Buffer controlled_buffer_3
  Decoder #(.select(2)) decoder_2 (
    .out0(decoder_2_out0), .out1(decoder_2_out1), .out2(decoder_2_out2), .sel(XY[1:0]), .en(undriven_2));  // open: out3
  assign H0 = decoder_2_out0 ? {clock, ID_symbol[0]} : 2'bz;  // Controlled_Buffer controlled_buffer_4
  assign H1 = decoder_2_out1 ? {clock, ID_symbol[0]} : 2'bz;  // Controlled_Buffer controlled_buffer_5
  assign H2 = decoder_2_out2 ? {clock, ID_symbol[0]} : 2'bz;  // Controlled_Buffer controlled_buffer_6
endmodule

// BBB
module BPC (
  input  H0,
  input  H1,
  input  H2,
  input  V0,
  input  V1,
  input  V2,
  input  reset,
  output [3:0] XY,
  output ready
);

  wire b_press, btn, H2_prime_out, nand_1_out, nand_2_out, pulse_rst_bus_0_2, V2_prime_out;
  wire [1:0] H0_prime_out, V0_prime_out;
  wire [3:0] coord;

  Pull_Resistor #(.pull(1)) pull_resistor_1 (.node(H2));
  Pull_Resistor #(.pull(1)) pull_resistor_2 (.node(H1));
  Pull_Resistor #(.pull(1)) pull_resistor_3 (.node(V2));
  Pull_Resistor #(.pull(1)) pull_resistor_4 (.node(V1));
  Pull_Resistor #(.pull(1)) pull_resistor_5 (.node(H0));
  Pull_Resistor #(.pull(1)) pull_resistor_6 (.node(V0));
  pulse pulse_rst (.bus_0(reset), .bus_0_2(pulse_rst_bus_0_2));
  nand nand_1 (nand_1_out, H0, H1, H2);
  and and_1 (b_press, nand_1_out, nand_2_out);
  pulse pls_btn (.bus_0(b_press), .bus_0_2(btn));
  nand nand_2 (nand_2_out, V0, V1, V2);
  // Probe on btn
  S_R_Flip_Flop #(.trigger("high")) ready_flag (
    .S(btn), .clk(1'b1), .R(pulse_rst_bus_0_2), .Qn(ready));  // open: Q, preset, reset, en
  // Probe on b_press
  nand H0_prime (H0_prime_out[0], V0, V1, ~V2);  // NAND_Gate
  nand H1_prime (H0_prime_out[1], V0, ~V1, V2);  // NAND_Gate
  nand H2_prime (H2_prime_out, ~V0, V1, V2);  // NAND_Gate
  nand V0_prime (V0_prime_out[0], H0, H1, ~H2);  // NAND_Gate
  nand V1_prime (V0_prime_out[1], H0, ~H1, H2);  // NAND_Gate
  nand V2_prime (V2_prime_out, ~H0, H1, H2);  // NAND_Gate
  Pull_Resistor pull_resistor_7 (.node(coord[3:2]));
  assign coord[3:2] = H2_prime_out ? H0_prime_out : 2'bz;  // Controlled_Buffer controlled_buffer_1
  // Probe on coord[3:2]
  // Probe on coord[1:0]
  Pull_Resistor pull_resistor_8 (.node(coord[1:0]));
  assign coord[1:0] = V2_prime_out ? V0_prime_out : 2'bz;  // Controlled_Buffer controlled_buffer_2
  Register #(.width(4)) XY_reg (.D(coord), .en(b_press), .Q(XY), .clk(b_press));  // open: clr

  // Other names for the same wires on the sheet: xcoord[2:0] = {V2, V1, V0}; ycoord[2:0] = {H2, H1, H0}

  // Notes on the sheet:
  //   3 Pull'ов, чтобы не было пересечений
  //   I/O Pins Inputs: H0, H1, H2, V0, V1, V2, reset Outputs: ready, XY(4)  - DONE
  //   b_press = (V0∧V1∧V2)’ ∧ (H0∧H1∧H2)’
  //   Internal Signals: xcoord(2), ycoord(2), XY(4), coord(4), b_press, btn, rst Latches: register(4) XY_reg, RS ready_flag
  //   Хитрая реализация представленного справа:
  //   coord.split(0:1) = ycoord
  //   coord.split(2:3) = xcoord
  //   Реализация модуля не сложная, если следовать инструкции.
  //   weak-if V0’ then 0b10
  //   weak-if V1’ then 0b01
  //   weak-if V2’ then 0b00
endmodule

// Tic Tac Toe
module TTTC (
  input  [1:0] hin,
  input  [1:0] vin,
  input  btn,
  input  reset,
  output hout,
  output [3:0] L0,
  output [3:0] L1,
  output vout,
  output [3:0] L2,
  output [3:0] L3,
  output [1:0] state
);

  wire and_1_out;

  and and_1 (and_1_out, hin[1], vin[1]);
  Register #(.width(2)) sym_reg (.D({hin[0], vin[0]}), .en(and_1_out), .Q(state), .clk(and_1_out), .clr(reset));
  ROM #(.addrWidth(2), .dataWidth(16)) rom_1 (.addr(state), .data({L3, L2, L1, L0}));  // open: sel
  Transistor #(.\type ("n"), .gate("br")) transistor_1 (.in(1'b0), .out(hout), .gate(btn));

  assign vout = hout;

  // Other names for the same wires on the sheet: addr[1:0] = state

  // Notes on the sheet:
  //   I/O Pins
  //    Inputs: vin(2), hin(2), btn 
  //   do: sym_reg := symID 
  //   Outputs: vout, hout, L0(4), L1(4), L2(4), L3(4) 
  //   sym ID
  //   on rising_edge of (hin.split(1) ∧ vin.split(1)) 
  //   addr = sym_reg
  //   ROM
  //   contents of rom_1 (hex, n*v repeats v):
  //   0 f99f 9429
  //   bitmap
  //   bitmap = symbols[addr]
  //   L0=bitmap.split (0:3)
  //   L1=bitmap.split (4:7)
  //   L2=bitmap.split (8:11)
  //   L3=bitmap.split (12:15)
  //   hout = if btn then 0 else float 
  //   vout = if btn then 0 else float
endmodule

// I win
module GSDD (
  input  [1:0] score,
  input  clock,
  input  reset,
  output win,
  output lose,
  output draw
);

  wire [1:0] state_q;

  Register #(.width(2)) state (.D(score), .en(clock), .Q(state_q), .clk(clock), .clr(reset));
  and u_win (win, ~state_q[0], state_q[1]);  // AND_Gate
  and u_lose (lose, state_q[0], ~state_q[1]);  // AND_Gate
  and u_draw (draw, state_q[0], state_q[1]);

  // Notes on the sheet:
  //   lose либо 00, либо 10. Проверить!
  //   lose = if state is 0b00 then 1 else 0
  //   win = if state is 0b01 then 1 else 0
  //   draw = if state is 0b11 then 1 else 0 
endmodule

module pulse (
  input  bus_0,
  output bus_0_2
);

  wire not_1_out;

  not not_1 (not_1_out, bus_0);
  nor nor_1 (bus_0_2, not_1_out, bus_0);
endmodule

module CdM_8 (
  input  [7:0] data_in,
  input  shadow,
  input  clk,
  input  IRQ,
  input  rset,
  input  [2:0] vector,
  output [7:0] PS,
  output [7:0] SP,
  output [2:0] page,
  output [7:0] PC,
  output data_code_prime,
  output [7:0] R3,
  output mem,
  output [7:0] R2,
  output load_st_prime,
  output [7:0] R1,
  output [7:0] R0,
  output [7:0] addr,
  output [7:0] data_out,
  output IAck
);

  wire add, addsp, alu_b, alu_u, alu_u1, and_2_out, and_3_out, and_4_out, and_5_out, and_6_out, and_7_out,
       and_8_out, and_9_out, and_11_out, and_13_out, and_16_out, and_17_out, and_18_out, and_19_out,
       and_20_out, and_21_out, and_22_out, auto, br_dcsn_1_go, br_nop, br_taken, Cl, cmp, crc,
       decoder_2_out3, decoder_5_out0, decoder_7_out0, decoder_7_out1, decoder_7_out2, decoder_7_out3,
       dwn_up_prime, Fetch, halt, \int , ioi, jsr, L_CVZN, L_tmpg, Latch, latchPC, latchPSR, ldc, ldi, ldsa,
       m_ld, m_st, nor_1_out, nor_2_out, nor_3_out, nor_4_out, not_2_out, not_3_out, not_4_out, not_5_out,
       not_8_out, not_int, odd, offset, or_1_out, or_2_out, or_3_out, or_4_out, or_5_out, or_7_out, or_8_out,
       or_9_out, or_10_out, or_11_out, or_13_out, osix, PC2b0, PC2b1, PCinc, pglk, Ph1, Ph1_plus, Ph2, Ph2_4,
       Ph3, Ph4, Ph5, Ph6, po, popall, PSR2b1, pu, pushall, Rd_as_src, RdA, RRA, rs_latch_3_q_prime, RsA,
       rti, rts, RX2b1, RX2pc, RXL, setsp, SP2b0, SP2b1, SPact, SPL, tmpg, tmpg2PSR, up_dwn_prime, vec,
       \wait ;
  wire [1:0] fun_u, iterator_1_rd, multiplexer_1_out;
  wire [2:0] adder_1_out, and_1_out, and_10_out, and_12_out, fun_b, multiplexer_2_out, multiplexer_5_out,
       register_1_q, register_3_q_2, vec_adr;
  wire [2:2] not_1_out;
  wire [3:0] alu_1_cvzn;
  wire [6:0] bit_extender_1_out;
  wire [7:0] alu_1_r, Instr, multiplexer_4_out, regfile_1_bus0o, register_3_q;

  Pull_Resistor pull_resistor_1 (.node(auto));
  Pull_Resistor pull_resistor_2 (.node(RsA));
  or or_1 (or_1_out, and_2_out, and_3_out, and_4_out, and_5_out, and_6_out, and_7_out);
  Multiplexer #(.width(2), .disabled(0), .enable("false")) multiplexer_1 (
    .in0(Instr[1:0]), .in1(iterator_1_rd), .out(multiplexer_1_out), .sel(or_2_out));
  or or_2 (or_2_out, auto, dwn_up_prime);
  Pull_Resistor pull_resistor_3 (.node(Rd_as_src));
  Pull_Resistor pull_resistor_4 (.node(latchPC));
  Pull_Resistor pull_resistor_5 (.node(PCinc));
  Pull_Resistor pull_resistor_6 (.node(PC2b1));
  Pull_Resistor pull_resistor_7 (.node(PC2b0));
  assign and_1_out = adder_1_out & {3{not_1_out[2]}};  // AND_Gate and_1, 3 bits wide
  not not_1 (not_1_out[2], or_1_out);
  Pull_Resistor pull_resistor_8 (.node(IRQ));
  iterator iterator_1 (.dec_inc_prime(dwn_up_prime), .enable(or_2_out), .Rd(iterator_1_rd), .Cl(Cl), .reset(rset));
  // Probe on iterator_1_rd
  Pull_Resistor pull_resistor_9 (.node(dwn_up_prime));
  assign data_in = alu_u1 ? alu_1_r : 8'bz;  // Controlled_Buffer controlled_buffer_1
  Pull_Resistor pull_resistor_10 (.node(RdA));
  Pull_Resistor pull_resistor_11 (.node(Latch));
  Register #(.width(3), .trigger("falling")) register_1 (
    .D(and_1_out), .en(not_2_out), .Q(register_1_q), .clk(Cl), .clr(rset));
  not not_2 (not_2_out, IAck);
  and and_2 (and_2_out, Ph1, nor_3_out);
  and and_3 (and_3_out, Ph2, nor_4_out);
  and and_4 (and_4_out, Ph3, ldsa);
  and and_5 (and_5_out, Ph4, popall);
  and and_6 (and_6_out, Ph5, or_3_out);
  and and_7 (and_7_out, Ph6, osix);
  not not_3 (not_3_out, IRQ);
  nor nor_1 (nor_1_out, not_3_out, IRQ);
  and and_8 (and_8_out, Fetch, not_4_out);
  not not_4 (not_4_out, Fetch);
  Pull_Resistor pull_resistor_12 (.node(alu_u1));
  Pull_Resistor pull_resistor_13 (.node(RX2pc));
  Pull_Resistor pull_resistor_14 (.node(RXL));
  or or_3 (or_3_out, ioi, pushall);
  or or_4 (or_4_out, rset, nor_1_out);
  and and_9 (and_9_out, IRQ, PS[7], and_8_out);
  not not_5 (not_5_out, Ph5);
  nor nor_2 (nor_2_out, not_5_out, Ph5);
  Pull_Resistor pull_resistor_15 (.node(RRA));
  Adder #(.width(3)) adder_1 (.a(register_1_q), .b(3'b000), .out(adder_1_out), .cin(1'b1));  // open: cout
  Decoder #(.select(3), .disabled(0), .enable("false")) decoder_1 (
    .out0(Fetch), .out1(Ph1), .out2(Ph2), .out3(Ph3), .out4(Ph4), .out5(Ph5), .out6(Ph6), .sel(register_1_q));  // open: out7
  nor nor_3 (nor_3_out, and_11_out, pu, jsr, or_7_out, crc, or_8_out, osix);
  nor nor_4 (nor_4_out, osix, ioi, ldsa, pushall, popall);
  RS_latch rs_latch_1 (.S(and_9_out), .R(or_4_out), .Q(IAck), .reset(rset));  // open: Q_prime
  or or_5 (or_5_out, nor_2_out, rset);
  Pull_Resistor pull_resistor_16 (.node(RX2b1));
  assign and_10_out = page & {3{shadow}};  // AND_Gate and_10, 3 bits wide
  or or_6 (Ph2_4, Ph4, Ph3, Ph2);
  RS_latch rs_latch_2 (.S(IAck), .R(or_5_out), .Q(\int ), .Q_prime(not_int), .reset(rset));
  Register #(.width(3), .trigger("falling")) register_2 (.D(vector), .Q(vec_adr), .clk(IAck), .clr(rset));  // open: en
  regfile regfile_1 (
    .RsSel(fun_u), .R0(R0), .Bus0o(regfile_1_bus0o), .RsAssert(RsA), .R1(R1), .R2(R2), .R3(R3),
    .UseRd_Rs_prime(Rd_as_src), .PC(PC), .RdSel(multiplexer_1_out), .SP(SP), .RdAssert(RdA), .latch(Latch),
    .Bus1(data_in), .Bus1o(data_in), .ALUres(alu_1_r), .latchPC(latchPC), .latchSP(SPL), .Cl(Cl),
    .rset(rset), .RR2bus1(RRA), .latchRX(RXL), .rx2pc_b12pc_prime(RX2pc), .PC2bus0(PC2b0), .SPact(SPact),
    .SP2bus1(SP2b1), .SP2bus0(SP2b0), .PCinc(PCinc), .PC2bus1(PC2b1), .up_down_prime(up_dwn_prime),
    .pg(and_10_out), .offset(offset), .rx2b1(RX2b1));
  Pull_Resistor pull_resistor_17 (.node(up_dwn_prime));
  Pull_Resistor pull_resistor_18 (.node(SPact));
  Pull_Resistor #(.pull(1)) pull_resistor_19 (.node(shadow));
  not not_6 (Ph1_plus, Fetch);
  and and_11 (and_11_out, ~cmp, alu_b);  // AND_Gate
  or or_7 (or_7_out, ioi, rti);
  or or_8 (or_8_out, pushall, ldsa, popall);
  assign and_12_out = {3{\int }} & vec_adr;  // AND_Gate and_12, 3 bits wide
  Pull_Resistor pull_resistor_20 (.node(odd));
  Pull_Resistor pull_resistor_21 (.node(SP2b0));
  Pull_Resistor pull_resistor_22 (.node(SP2b1));
  Pull_Resistor pull_resistor_23 (.node(offset));
  Pull_Resistor pull_resistor_24 (.node(SPL));
  Pull_Resistor pull_resistor_25 (.node(vec));
  Multiplexer #(.select(2), .width(3), .disabled(0), .enable("false")) multiplexer_2 (
    .in0(fun_b), .in1({fun_b[0], fun_u}), .in2(3'b001), .in3(3'b001), .out(multiplexer_2_out),
    .sel({add, alu_u}));
  Pull_Resistor pull_resistor_26 (.node(data_code_prime));
  Pull_Resistor pull_resistor_27 (.node(mem));
  Pull_Resistor pull_resistor_28 (.node(load_st_prime));
  Multiplexer #(.width(8), .enable("false")) multiplexer_3 (
    .in0(regfile_1_bus0o), .in1({4'b1111, and_12_out, odd}), .out(addr), .sel(vec));
  ALU alu_1 (
    .fun(multiplexer_2_out), .u_b_prime(and_13_out), .X(regfile_1_bus0o), .Y(data_in), .CVZN(alu_1_cvzn),
    .R(alu_1_r), .C(PS[3]));
  // Probe on alu_1_r
  and and_13 (and_13_out, ~add, alu_u);  // AND_Gate
  Pull_Resistor pull_resistor_29 (.node(add));
  and and_14 (cmp, ~Instr[7], fun_b[2], fun_b[1], fun_b[0]);  // AND_Gate
  and and_15 (alu_u, Instr[7], ~fun_b[2], ~fun_b[1]);  // AND_Gate
  Pull_Resistor pull_resistor_30 (.node(latchPSR));
  Pull_Resistor pull_resistor_31 (.node(L_CVZN));
  Decoder #(.select(2), .disabled(0)) decoder_2 (
    .out0(pu), .out1(po), .out2(ldsa), .out3(decoder_2_out3), .sel(fun_u), .en(and_16_out));
  and and_16 (and_16_out, Instr[7], fun_b[2], ~fun_b[1], ~fun_b[0]);  // AND_Gate
  not not_7 (alu_b, Instr[7]);
  and and_17 (and_17_out, Instr[7], ~fun_b[2], fun_b[1]);  // AND_Gate
  Decoder #(.disabled(0)) decoder_3 (.out0(m_st), .out1(m_ld), .sel(fun_b[0]), .en(and_17_out));
  and and_18 (and_18_out, ~halt, clk, IRQ);  // AND_Gate
  Bit_Extender #(.out_width(7)) bit_extender_1 (.in(data_in), .out(bit_extender_1_out));
  PS ps_1 (
    .ldPS(latchPSR), .CVZN(alu_1_cvzn), .bus_in(multiplexer_4_out), .latch_CVZN(L_CVZN), .bus_out(data_in),
    .\assert (PSR2b1), .Output(PS), .Cl(Cl), .Rset(rset));
  and and_19 (and_19_out, fun_b[1], fun_b[2], Instr[7]);
  and and_20 (and_20_out, clk, Ph1, or_9_out);
  or or_9 (or_9_out, \wait , halt);
  or or_10 (or_10_out, and_18_out, rset);
  IR ir_1 (
    .latch(Fetch), .Cl(Cl), .Reset(rset), .Output({Instr[7], fun_b, fun_u, Instr[1:0]}), .\input (data_in),
    .\int (\int ));
  Pull_Resistor pull_resistor_32 (.node(L_tmpg));
  Register #(.width(7), .trigger("falling")) register_3 (
    .D(bit_extender_1_out), .en(L_tmpg), .Q({register_3_q_2, register_3_q[3:0]}), .clk(Cl), .clr(or_11_out));
  or or_11 (or_11_out, rset, ioi);
  Pull_Resistor pull_resistor_33 (.node(PSR2b1));
  Decoder #(.select(2), .disabled(0)) decoder_4 (
    .out0(addsp), .out1(setsp), .out2(pushall), .out3(popall), .sel(Instr[1:0]), .en(decoder_2_out3));
  and and_21 (and_21_out, Instr[7], fun_b[2], ~fun_b[1], fun_b[0]);  // AND_Gate
  Decoder #(.disabled(0)) decoder_5 (.out0(decoder_5_out0), .out1(ldc), .sel(fun_b[0]), .en(and_19_out));
  Decoder #(.disabled(0)) decoder_6 (.out0(br_nop), .out1(br_taken), .sel(br_dcsn_1_go), .en(decoder_5_out0));
  not not_8 (not_8_out, and_20_out);
  and and_22 (and_22_out, and_20_out, not_8_out);
  RS_latch rs_latch_3 (.S(and_22_out), .R(or_10_out), .Q_prime(rs_latch_3_q_prime), .reset(rset));  // open: Q
  Multiplexer #(.width(8), .enable("false")) multiplexer_4 (
    .in0(data_in), .in1({register_3_q[7], register_3_q_2, register_3_q[3:0]}), .out(multiplexer_4_out),
    .sel(tmpg2PSR));
  Decoder #(.select(4), .disabled(0)) decoder_7 (
    .out0(decoder_7_out0), .out1(decoder_7_out1), .out2(decoder_7_out2), .out3(decoder_7_out3), .out4(halt),
    .out5(\wait ), .out6(jsr), .out7(rts), .out8(ioi), .out9(rti), .out10(crc), .out11(osix),
    .sel({fun_u, Instr[1:0]}), .en(and_21_out));  // open: out12, out13, out14, out15
  br_dcsn br_dcsn_1 (.cccc({fun_u, Instr[1:0]}), .CVZN(PS[3:0]), .go(br_dcsn_1_go));
  and and_23 (Cl, clk, rs_latch_3_q_prime);
  Pull_Resistor pull_resistor_34 (.node(register_3_q[7]));
  buf buffer_1 (register_3_q[7], data_in[7]);
  Pull_Resistor pull_resistor_35 (.node(tmpg2PSR));
  or or_12 (ldi, decoder_7_out0, decoder_7_out1, decoder_7_out2, decoder_7_out3);
  Register #(.width(3), .trigger("low")) register_4 (.D(multiplexer_5_out), .Q(page), .clk(pglk));  // open: en, clr
  Multiplexer #(.width(3), .disabled(0), .enable("false")) multiplexer_5 (
    .in0(PS[6:4]), .in1(register_3_q_2), .out(multiplexer_5_out), .sel(tmpg));
  Pull_Resistor pull_resistor_36 (.node(tmpg));
  Pull_Resistor pull_resistor_37 (.node(pglk));
  _6driver u_6driver_1 (
    .in_1(jsr), .in_2(Ph1), .out_3(SPact), .out_4(PC2b0), .out_5(mem), .out_6(load_st_prime), .out_7(RXL),
    .out_8(PCinc));
  _6driver u_6driver_2 (
    .in_1(osix), .in_2(Ph4), .out_3(SP2b0), .out_4(mem), .out_5(data_code_prime), .out_6(PSR2b1), .out_7(tmpg));  // open: out_8
  _4driver u_4driver_1 (.in_1(alu_b), .in_2(Ph1), .out_3(RsA), .out_4(RdA), .out_6(L_CVZN));  // open: out_5
  _6driver u_6driver_3 (
    .in_1(m_ld), .in_2(Ph1), .out_3(RsA), .out_4(Latch), .out_5(load_st_prime), .out_6(mem),
    .out_8(data_code_prime));  // open: out_7
  _6driver u_6driver_4 (
    .in_1(setsp), .in_2(Ph1), .out_3(PC2b0), .out_4(mem), .out_5(load_st_prime), .out_6(SPL), .out_8(PCinc));  // open: out_7
  _2driver u_2driver_1 (.in_1(ldsa), .in_2(Ph3), .out_3(Latch), .out_4(RRA));
  _4driver u_4driver_2 (.in_1(ldsa), .in_2(Ph2), .out_3(RdA), .out_4(add), .out_5(SP2b0));  // open: out_6
  _6driver u_6driver_5 (
    .in_1(ldsa), .in_2(Ph1), .out_3(PC2b0), .out_4(mem), .out_5(load_st_prime), .out_6(Latch), .out_8(PCinc));  // open: out_7
  _2driver u_2driver_2 (.in_1(br_nop), .in_2(Ph1), .out_3(PCinc));  // open: out_4
  _6driver u_6driver_6 (
    .in_1(osix), .in_2(Ph1), .out_4(PC2b0), .out_5(PCinc), .out_6(load_st_prime), .out_7(mem), .out_8(L_tmpg));  // open: out_3
  _2driver u_2driver_3 (.in_1(ioi), .in_2(Ph1), .out_3(SPact), .out_4(tmpg));
  _6driver u_6driver_7 (
    .in_1(ioi), .in_2(Ph4), .out_3(vec), .out_4(latchPC), .out_5(load_st_prime), .out_6(mem), .out_7(tmpg));  // open: out_8
  _6driver u_6driver_8 (
    .in_1(ioi), .in_2(Ph2), .out_3(SP2b0), .out_4(data_code_prime), .out_5(mem), .out_6(PC2b1),
    .out_7(SPact), .out_8(tmpg));
  _2driver u_2driver_4 (.in_1(alu_b), .in_2(Ph2), .out_3(Latch), .out_4(RRA));
  _6driver u_6driver_9 (
    .in_1(m_st), .in_2(Ph1), .out_3(RsA), .out_4(RdA), .out_5(mem), .out_6(data_code_prime));  // open: out_7, out_8
  _6driver u_6driver_10 (
    .in_1(addsp), .in_2(Ph1), .out_3(PC2b0), .out_4(mem), .out_5(load_st_prime), .out_6(SPL), .out_7(offset),
    .out_8(PCinc));
  _8driver u_8driver_1 (
    .in_1(popall), .in_2(Ph1_plus), .out_3(SP2b0), .out_4(mem), .out_5(load_st_prime), .out_6(Latch),
    .out_7(SPact), .out_8(up_dwn_prime), .out_9(data_code_prime), .out_10(auto));
  _8driver u_8driver_2 (
    .in_1(po), .in_2(Ph1), .out_3(SP2b0), .out_4(mem), .out_5(load_st_prime), .out_6(Latch), .out_7(SPact),
    .out_8(up_dwn_prime), .out_9(data_code_prime));  // open: out_10
  _4driver u_4driver_3 (
    .in_1(br_taken), .in_2(Ph1), .out_3(PC2b0), .out_4(mem), .out_5(load_st_prime), .out_6(latchPC));
  _6driver u_6driver_11 (
    .in_1(jsr), .in_2(Ph2), .out_3(PC2b1), .out_4(SP2b0), .out_5(mem), .out_6(data_code_prime), .out_7(RX2pc));  // open: out_8
  _2driver u_2driver_5 (.in_1(osix), .in_2(Ph2), .out_3(SPact), .out_4(tmpg));
  _6driver u_6driver_12 (
    .in_1(osix), .in_2(Ph5), .out_3(vec), .out_4(latchPC), .out_5(load_st_prime), .out_6(mem), .out_7(tmpg));  // open: out_8
  _6driver u_6driver_13 (
    .in_1(osix), .in_2(Ph3), .out_3(SP2b0), .out_4(data_code_prime), .out_5(mem), .out_6(PC2b1),
    .out_7(SPact), .out_8(tmpg));
  _6driver u_6driver_14 (
    .in_1(ioi), .in_2(Ph3), .out_3(SP2b0), .out_4(mem), .out_5(data_code_prime), .out_6(PSR2b1), .out_7(tmpg));  // open: out_8
  _6driver u_6driver_15 (
    .in_1(ioi), .in_2(Ph5), .out_3(vec), .out_4(odd), .out_5(load_st_prime), .out_6(mem), .out_7(tmpg),
    .out_8(latchPSR));
  _6driver u_6driver_16 (
    .in_1(alu_u), .in_2(Ph1), .out_3(RsA), .out_4(Rd_as_src), .out_5(Latch), .out_6(L_CVZN), .out_8(alu_u1));  // open: out_7
  _4driver u_4driver_4 (.in_1(ldc), .in_2(Ph1), .out_3(RsA), .out_4(Latch), .out_5(load_st_prime), .out_6(mem));
  _6driver u_6driver_17 (
    .in_1(crc), .in_2(Ph1), .out_3(SP2b0), .out_4(mem), .out_5(load_st_prime), .out_7(data_code_prime),
    .out_8(RXL));  // open: out_6
  _4driver u_4driver_5 (.in_1(Fetch), .in_2(not_int), .out_3(PC2b0), .out_4(load_st_prime), .out_5(mem), .out_6(PCinc));
  _6driver u_6driver_18 (
    .in_1(Ph5), .in_2(pushall), .out_3(SP2b0), .out_4(RdA), .out_5(mem), .out_6(data_code_prime),
    .out_8(dwn_up_prime));  // open: out_7
  _6driver u_6driver_19 (
    .in_1(Ph2_4), .in_2(pushall), .out_3(SP2b0), .out_4(RdA), .out_5(mem), .out_6(data_code_prime),
    .out_7(SPact), .out_8(dwn_up_prime));
  _6driver u_6driver_20 (
    .in_1(Ph2), .in_2(pu), .out_3(SP2b0), .out_4(RdA), .out_5(mem), .out_6(data_code_prime));  // open: out_7, out_8
  _8driver u_8driver_3 (
    .in_1(rts), .in_2(Ph1), .out_3(SP2b0), .out_4(up_dwn_prime), .out_5(SPact), .out_6(mem),
    .out_7(load_st_prime), .out_8(data_code_prime), .out_9(latchPC));  // open: out_10
  _8driver u_8driver_4 (
    .in_1(osix), .in_2(Ph6), .out_3(vec), .out_4(odd), .out_5(load_st_prime), .out_6(mem), .out_7(tmpg2PSR),
    .out_8(latchPSR), .out_10(tmpg));  // open: out_9
  _6driver u_6driver_21 (
    .in_1(ldi), .in_2(Ph1), .out_3(PC2b0), .out_4(mem), .out_5(load_st_prime), .out_6(Latch), .out_8(PCinc));  // open: out_7
  or or_13 (or_13_out, pushall, pu);
  _2driver u_2driver_6 (.in_1(or_13_out), .in_2(Ph1), .out_3(SPact));  // open: out_4
  _6driver u_6driver_22 (
    .in_1(crc), .in_2(Ph2), .out_3(SP2b0), .out_4(mem), .out_5(PC2b1), .out_6(data_code_prime), .out_7(RX2pc));  // open: out_8
  _8driver u_8driver_5 (
    .in_1(rti), .in_2(Ph1), .out_3(SP2b0), .out_4(data_code_prime), .out_5(mem), .out_6(load_st_prime),
    .out_7(SPact), .out_8(up_dwn_prime), .out_9(pglk), .out_10(latchPSR));
  _8driver u_8driver_6 (
    .in_1(rti), .in_2(Ph2), .out_3(SP2b0), .out_4(latchPC), .out_5(mem), .out_6(load_st_prime),
    .out_7(SPact), .out_8(up_dwn_prime), .out_9(data_code_prime), .out_10(pglk));

  assign data_out = data_in;

  // Other names for the same wires on the sheet: Rd[1:0] = Instr[1:0]; Instr[6:2] = {fun_b, fun_u}; Rs[1:0] = fun_u;
  //   PShi[3:0] = PS[7:4]; data = data_code_prime; fun_u[2] = fun_b[0]; hold = IAck; ld = load_st_prime;
  //   CVZN[3:0] = PS[3:0]

  // Notes on the sheet:
  //   IRQ: pull=down
  //   popall/pushall indexer
  //   Sequencer
  //   Interrupt Master
  //   Data Path
  //   int. granted
  //   interrupt
  //   in progress
  //   (add)
  //   temporary page
  //   Coco-de-Mer-8 (Mark 4)
  //   page trap
  //   Primary Decoder
  //   Halt/wait logic
  //   ALU 2-op
  //   ld
  //   setsp
  //   ldsa
  //   br not taken
  //   jsr
  //   osix
  //   ioi
  //   Secondary Decoder
  //   st
  //   addsp
  //   popall
  //   pop
  //   br taken
  //   crc
  //   ALU 1-op
  //   ldc
  //   rts
  //   pushall
  //   push
  //   rti
  //   ldi
  //   Fetch
  //   ALU
  //   Memory
  //   Stack
  //   Ctrl
  //   Interrupts
endmodule

module Reg (
  input  asrt0,
  input  [7:0] \input ,
  input  latch,
  input  asrt1,
  input  Cl,
  input  Reset,
  output [7:0] mon,
  output [7:0] out0,
  output [7:0] out1
);

  Register #(.trigger("falling")) register_1 (.D(\input ), .en(latch), .Q(mon), .clk(Cl), .clr(Reset));
  assign out0 = asrt0 ? mon : 8'bz;  // Controlled_Buffer controlled_buffer_1
  assign out1 = asrt1 ? mon : 8'bz;  // Controlled_Buffer controlled_buffer_2

  // Notes on the sheet:
  //   input: pull=down
  //   Note: the library component "register" above
  //   is a replacement of 8D-latch and functions  identifcally
endmodule

// mux2
module mux2x1 (
  input  [7:0] in0,
  input  select,
  input  [7:0] in1,
  output [7:0] out
);

  wire [7:0] and_1_out, and_2_out;
  wire [7:7] not_1_out;

  not not_1 (not_1_out[7], select);
  assign and_1_out = in0 & {8{not_1_out[7]}};  // AND_Gate and_1, 8 bits wide
  assign and_2_out = {8{select}} & in1;  // AND_Gate and_2, 8 bits wide
  assign out = and_1_out | and_2_out;  // OR_Gate or_1, 8 bits wide

  // Notes on the sheet:
  //   in1: pull=down
  //   in0: pull=down
endmodule

module PC (
  input  asrt0,
  input  inc,
  input  [7:0] \input ,
  input  latch,
  input  asrt1,
  input  Cl,
  input  Reset,
  output [7:0] mon,
  output [7:0] out0,
  output [7:0] out1
);

  wire or_1_out;
  wire [7:0] adder_1_out, controlled_buffer_1_out;

  assign controlled_buffer_1_out = inc ? adder_1_out : 8'bz;  // Controlled_Buffer controlled_buffer_1
  assign controlled_buffer_1_out = latch ? \input  : 8'bz;  // Controlled_Buffer controlled_buffer_2
  or or_1 (or_1_out, inc, latch);
  Register #(.trigger("falling")) register_1 (
    .D(controlled_buffer_1_out), .en(or_1_out), .Q(mon), .clk(Cl), .clr(Reset));
  Adder adder_1 (.a({8{1'b0}}), .b(mon), .out(adder_1_out), .cin(1'b1));  // open: cout
  assign out0 = asrt0 ? mon : 8'bz;  // Controlled_Buffer controlled_buffer_3
  assign out1 = asrt1 ? mon : 8'bz;  // Controlled_Buffer controlled_buffer_4

  // Notes on the sheet:
  //   input: pull=down
endmodule

module SP (
  input  up_down_prime,
  input  offset,
  input  asrt0,
  input  step,
  input  [7:0] \input ,
  input  latch,
  input  asrt1,
  input  Cl,
  input  Reset,
  input  [2:0] pg,
  output [7:0] out0,
  output [7:0] out1,
  output [7:0] mon
);

  wire decoder_1_out0, decoder_1_out1, decoder_1_out2, decoder_1_out3, decoder_1_out4, decoder_1_out5,
       decoder_1_out6, decoder_1_out7, or_1_out;
  wire [7:0] adder_1_out, adder_2_out, controlled_buffer_1_out, multiplexer_1_out, register_1_q,
       register_2_q, register_3_q, register_4_q, register_5_q, register_6_q, register_7_q, register_8_q;
  wire [7:7] not_1_out;

  assign controlled_buffer_1_out = step ? adder_2_out : 8'bz;  // Controlled_Buffer controlled_buffer_1
  assign controlled_buffer_1_out = latch ? \input  : 8'bz;  // Controlled_Buffer controlled_buffer_2
  not not_1 (not_1_out[7], up_down_prime);
  Adder adder_1 (.a(controlled_buffer_1_out), .b(mon), .out(adder_1_out));  // open: cin, cout
  or or_1 (or_1_out, step, latch);
  Decoder #(.select(3), .disabled(0)) decoder_1 (
    .out0(decoder_1_out0), .out1(decoder_1_out1), .out2(decoder_1_out2), .out3(decoder_1_out3),
    .out4(decoder_1_out4), .out5(decoder_1_out5), .out6(decoder_1_out6), .out7(decoder_1_out7), .sel(pg),
    .en(or_1_out));
  Multiplexer #(.width(8), .enable("false")) multiplexer_1 (
    .in0(controlled_buffer_1_out), .in1(adder_1_out), .out(multiplexer_1_out), .sel(offset));
  Register #(.trigger("falling")) register_1 (
    .D(multiplexer_1_out), .en(decoder_1_out0), .Q(register_1_q), .clk(Cl), .clr(Reset));
  Register #(.trigger("falling")) register_2 (
    .D(multiplexer_1_out), .en(decoder_1_out1), .Q(register_2_q), .clk(Cl), .clr(Reset));
  Register #(.trigger("falling")) register_3 (
    .D(multiplexer_1_out), .en(decoder_1_out2), .Q(register_3_q), .clk(Cl), .clr(Reset));
  Register #(.trigger("falling")) register_4 (
    .D(multiplexer_1_out), .en(decoder_1_out3), .Q(register_4_q), .clk(Cl), .clr(Reset));
  Register #(.trigger("falling")) register_5 (
    .D(multiplexer_1_out), .en(decoder_1_out4), .Q(register_5_q), .clk(Cl), .clr(Reset));
  Register #(.trigger("falling")) register_6 (
    .D(multiplexer_1_out), .en(decoder_1_out5), .Q(register_6_q), .clk(Cl), .clr(Reset));
  Register #(.trigger("falling")) register_7 (
    .D(multiplexer_1_out), .en(decoder_1_out6), .Q(register_7_q), .clk(Cl), .clr(Reset));
  Register #(.trigger("falling")) register_8 (
    .D(multiplexer_1_out), .en(decoder_1_out7), .Q(register_8_q), .clk(Cl), .clr(Reset));
  Multiplexer #(.select(3), .width(8), .disabled(0), .enable("false")) multiplexer_2 (
    .in0(register_1_q), .in1(register_2_q), .in2(register_3_q), .in3(register_4_q), .in4(register_5_q),
    .in5(register_6_q), .in6(register_7_q), .in7(register_8_q), .out(mon), .sel(pg));
  Adder adder_2 (.a({{7{not_1_out[7]}}, 1'b1}), .b(mon), .out(adder_2_out), .cin(1'b0));  // open: cout
  assign out0 = asrt0 ? mon : 8'bz;  // Controlled_Buffer controlled_buffer_3
  assign out1 = asrt1 ? mon : 8'bz;  // Controlled_Buffer controlled_buffer_4

  // Notes on the sheet:
  //   input: pull=down
endmodule

module regfile (
  input  [1:0] RsSel,
  input  RsAssert,
  input  UseRd_Rs_prime,
  input  [2:0] pg,
  input  [1:0] RdSel,
  input  RdAssert,
  input  latch,
  input  [7:0] Bus1,
  input  [7:0] ALUres,
  input  offset,
  input  rx2b1,
  input  latchPC,
  input  latchSP,
  input  Cl,
  input  rset,
  input  RR2bus1,
  input  latchRX,
  input  rx2pc_b12pc_prime,
  input  PC2bus0,
  input  SPact,
  input  SP2bus1,
  input  SP2bus0,
  input  PCinc,
  input  PC2bus1,
  input  up_down_prime,
  output [7:0] R0,
  output [7:0] Bus0o,
  output [7:0] R1,
  output [7:0] R2,
  output [7:0] R3,
  output [7:0] PC,
  output [7:0] SP,
  output [7:0] Bus1o
);

  wire decoder_1_out0, decoder_1_out1, decoder_1_out2, decoder_1_out3, decoder_2_out0, decoder_2_out1,
       decoder_2_out2, decoder_2_out3, decoder_3_out0, decoder_3_out1, decoder_3_out2, decoder_3_out3,
       not_1_out, or_1_out, or_2_out;
  wire [1:0] multiplexer_1_out;
  wire [7:0] controlled_buffer_1_out, multiplexer_2_out, reg_6_out0;

  Decoder #(.select(2), .disabled(0)) decoder_1 (
    .out0(decoder_1_out0), .out1(decoder_1_out1), .out2(decoder_1_out2), .out3(decoder_1_out3),
    .sel(multiplexer_1_out), .en(RsAssert));
  Multiplexer #(.width(2), .enable("false")) multiplexer_1 (
    .in0(RsSel), .in1(RdSel), .out(multiplexer_1_out), .sel(UseRd_Rs_prime));
  Decoder #(.select(2), .disabled(0)) decoder_2 (
    .out0(decoder_2_out0), .out1(decoder_2_out1), .out2(decoder_2_out2), .out3(decoder_2_out3), .sel(RdSel),
    .en(RdAssert));
  Decoder #(.select(2), .disabled(0)) decoder_3 (
    .out0(decoder_3_out0), .out1(decoder_3_out1), .out2(decoder_3_out2), .out3(decoder_3_out3), .sel(RdSel),
    .en(latch));
  assign controlled_buffer_1_out = not_1_out ? Bus1 : 8'bz;  // Controlled_Buffer controlled_buffer_1
  Reg reg_1 (
    .asrt0(decoder_1_out0), .out0(Bus0o), .\input (controlled_buffer_1_out), .latch(decoder_3_out0),
    .out1(controlled_buffer_1_out), .asrt1(decoder_2_out0), .Cl(Cl), .Reset(rset), .mon(R0));
  or or_1 (or_1_out, RdAssert, PC2bus1, SP2bus1, RR2bus1, rx2b1);
  not not_1 (not_1_out, or_1_out);
  Reg reg_2 (
    .asrt0(decoder_1_out1), .out0(Bus0o), .\input (controlled_buffer_1_out), .latch(decoder_3_out1),
    .out1(controlled_buffer_1_out), .asrt1(decoder_2_out1), .Cl(Cl), .Reset(rset), .mon(R1));
  Reg reg_3 (
    .asrt0(decoder_1_out2), .out0(Bus0o), .\input (controlled_buffer_1_out), .latch(decoder_3_out2),
    .out1(controlled_buffer_1_out), .asrt1(decoder_2_out2), .Cl(Cl), .Reset(rset), .mon(R2));
  Reg reg_4 (
    .asrt0(decoder_1_out3), .out0(Bus0o), .\input (controlled_buffer_1_out), .latch(decoder_3_out3),
    .out1(controlled_buffer_1_out), .asrt1(decoder_2_out3), .Cl(Cl), .Reset(rset), .mon(R3));
  Reg reg_5 (
    .asrt0(1'b0), .\input (ALUres), .latch(1'b1), .out1(controlled_buffer_1_out), .asrt1(RR2bus1), .Cl(Cl),
    .Reset(rset));  // open: out0, mon
  Reg reg_6 (
    .asrt0(rx2pc_b12pc_prime), .out0(reg_6_out0), .\input (controlled_buffer_1_out), .latch(latchRX),
    .out1(controlled_buffer_1_out), .asrt1(rx2b1), .Cl(Cl), .Reset(rset));  // open: mon
  Pull_Resistor pull_resistor_1 (.node(rx2b1));
  Multiplexer #(.width(8), .enable("false")) multiplexer_2 (
    .in0(controlled_buffer_1_out), .in1(reg_6_out0), .out(multiplexer_2_out), .sel(rx2pc_b12pc_prime));
  or or_2 (or_2_out, rx2pc_b12pc_prime, latchPC);
  PC pc_1 (
    .inc(PCinc), .latch(or_2_out), .asrt0(PC2bus0), .out0(Bus0o), .out1(controlled_buffer_1_out),
    .asrt1(PC2bus1), .Cl(Cl), .\input (multiplexer_2_out), .Reset(rset), .mon(PC));
  SP sp_1 (
    .up_down_prime(up_down_prime), .step(SPact), .\input (controlled_buffer_1_out), .latch(latchSP),
    .asrt0(SP2bus0), .out0(Bus0o), .out1(controlled_buffer_1_out), .asrt1(SP2bus1), .mon(SP), .Cl(Cl),
    .Reset(rset), .pg(pg), .offset(offset));
  assign Bus1o = or_1_out ? controlled_buffer_1_out : 8'bz;  // Controlled_Buffer controlled_buffer_2

  // Other names for the same wires on the sheet: pc2b1 = PC2bus1; RdA = RdAssert; rr2b1 = RR2bus1; sp2b1 = SP2bus1

  // Notes on the sheet:
  //   ALUres: pull=down
  //   PCinc: pull=down
endmodule

// 2x4
module decoder_2x4 (
  input  [1:0] in,
  input  en,
  output [3:0] out
);

  wire not_1_out, not_2_out, not_3_out, not_4_out;

  not not_1 (not_1_out, in[1]);
  not not_2 (not_2_out, in[0]);
  not not_3 (not_3_out, in[1]);
  not not_4 (not_4_out, in[0]);
  and and_1 (out[0], not_1_out, en, not_2_out);
  and and_2 (out[1], not_3_out, en, in[0]);
  and and_3 (out[2], in[1], en, not_4_out);
  and and_4 (out[3], in[1], en, in[0]);
endmodule

module ALU (
  input  [2:0] fun,
  input  u_b_prime,
  input  C,
  input  [7:0] X,
  input  [7:0] Y,
  output [3:0] CVZN,
  output [7:0] R
);

  wire add, addc, adder_1_cout, and_2_out, and_3_out, and_4_out, and_5_out, and_6_out, and_9_out, and_10_out,
       arith, cmp, dec, inc, \logic , move, neg, \not , not_1_out, not_2_out, not_3_out, not_4_out,
       not_5_out, or_5_out, or_6_out, shift, sub, xor_1_out, xor_4_out, xor_5_out;
  wire [0:0] and_1_out;
  wire [2:0] decoder_2x4_1_out;
  wire [7:0] adder_1_out, bin_logic_1_result, controlled_buffer_6_out, mux2x1_1_out, xor_2_out, xor_3_out;
  wire [7:7] or_1_out, or_3_out, or_4_out;

  and and_1 (and_1_out[0], X[7], fun[1]);
  and and_2 (and_2_out, X[7], fun[1]);
  not not_1 (not_1_out, fun[1]);
  and and_3 (and_3_out, not_1_out, C);
  decoder_2x4 decoder_2x4_1 (.in({u_b_prime, fun[2]}), .en(1'b1), .out({shift, decoder_2x4_1_out}));
  or or_1 (or_1_out[7], and_2_out, and_3_out);
  xor xor_1 (xor_1_out, X[6], X[7]);
  not not_2 (not_2_out, fun[1]);
  or or_2 (arith, decoder_2x4_1_out[2], decoder_2x4_1_out[0], cmp);
  and and_4 (and_4_out, xor_1_out, fun[0], not_2_out);
  decoder_2x4 decoder_2x4_2 (.in(fun[1:0]), .en(decoder_2x4_1_out[0]), .out({sub, addc, add, move}));
  decoder_2x4 decoder_2x4_3 (.in(fun[1:0]), .en(decoder_2x4_1_out[2]), .out({inc, dec, neg, \not }));
  mux2x1 mux2x1_1 (.in0({or_1_out[7], X[7:1]}), .select(fun[0]), .in1({X[6:0], and_1_out[0]}), .out(mux2x1_1_out));
  assign CVZN[2] = shift ? and_4_out : 1'bz;  // Controlled_Buffer controlled_buffer_1
  assign {CVZN[0], R[6:0]} = shift ? mux2x1_1_out : 8'bz;  // Controlled_Buffer controlled_buffer_2
  and and_5 (and_5_out, not_3_out, shift);
  not not_3 (not_3_out, fun[0]);
  assign CVZN[3] = and_5_out ? X[0] : 1'bz;  // Controlled_Buffer controlled_buffer_3
  assign CVZN[3] = and_6_out ? X[7] : 1'bz;  // Controlled_Buffer controlled_buffer_4
  and and_6 (and_6_out, fun[0], shift);
  not not_4 (not_4_out, cmp);
  and and_7 (cmp, fun[0], fun[1], decoder_2x4_1_out[1]);
  and and_8 (\logic , decoder_2x4_1_out[1], not_4_out);
  // Probe on bin_logic_1_result
  bin_logic bin_logic_1 (.op1(X), .op2(Y), .or_and_prime(fun[0]), .xor_and_prime(fun[1]), .result(bin_logic_1_result));
  assign {CVZN[0], R[6:0]} = \logic  ? bin_logic_1_result : 8'bz;  // Controlled_Buffer controlled_buffer_5
  or or_3 (or_3_out[7], cmp, sub);
  or or_4 (or_4_out[7], \not , neg);
  and and_9 (and_9_out, C, addc);
  or or_5 (or_5_out, or_3_out[7], addc, add);
  assign xor_2_out = Y ^ {8{or_3_out[7]}};  // XOR_Gate xor_2, 8 bits wide
  assign xor_3_out = X ^ {8{or_4_out[7]}};  // XOR_Gate xor_3, 8 bits wide
  or or_6 (or_6_out, neg, and_9_out, or_3_out[7]);
  assign controlled_buffer_6_out = or_5_out ? xor_2_out : 8'bz;  // Controlled_Buffer controlled_buffer_6
  nor nor_1 (CVZN[1], R[0], R[1], R[2], R[3], R[4], R[5], R[6], CVZN[0]);
  Pull_Resistor pull_resistor_1 (.node(CVZN[3]));
  Pull_Resistor pull_resistor_2 (.node(CVZN[2]));
  Adder adder_1 (.a(xor_3_out), .b(controlled_buffer_6_out), .out(adder_1_out), .cin(or_6_out), .cout(adder_1_cout));
  assign controlled_buffer_6_out = inc ? 8'h1 : 8'bz;  // Controlled_Buffer controlled_buffer_7
  assign {CVZN[0], R[6:0]} = arith ? adder_1_out : 8'bz;  // Controlled_Buffer controlled_buffer_8
  assign CVZN[3] = arith ? adder_1_cout : 1'bz;  // Controlled_Buffer controlled_buffer_9
  assign controlled_buffer_6_out = dec ? {8{1'b1}} : 8'bz;  // Controlled_Buffer controlled_buffer_10
  Pull_Resistor pull_resistor_3 (.node(controlled_buffer_6_out));
  xor xor_4 (xor_4_out, controlled_buffer_6_out[7], xor_3_out[7]);
  not not_5 (not_5_out, xor_4_out);
  and and_10 (and_10_out, not_5_out, xor_5_out);
  assign CVZN[2] = arith ? and_10_out : 1'bz;  // Controlled_Buffer controlled_buffer_11
  xor xor_5 (xor_5_out, xor_3_out[7], adder_1_out[7]);

  assign R[7] = CVZN[0];

  // Other names for the same wires on the sheet: Snew = X[6]; S = X[7]; V = CVZN[2]; Cout = CVZN[3];
  //   logop[1:0] = fun[1:0]; low[1:0] = fun[1:0]; J = X[0]

  // Notes on the sheet:
  //   Y: pull=down
  //   X: pull=down
  //   R: pull=down
  //   Decoder
  //   if shr then C
  //   Shifts
  //   elseif shra then X7
  //   Binary logic ops
  //   Binary and unary arithmetic ops
  //   Condition codes
  //   Pins
endmodule

// &VX
module bin_logic (
  input  [7:0] op1,
  input  [7:0] op2,
  input  or_and_prime,
  input  xor_and_prime,
  output [7:0] result
);

  wire [7:0] and_1_out, and_2_out, and_3_out, and_4_out, and_5_out, or_1_out, xor_1_out;
  wire [7:7] not_1_out;

  not not_1 (not_1_out[7], xor_and_prime);
  assign xor_1_out = op1 ^ op2;  // XOR_Gate xor_1, 8 bits wide
  assign and_1_out = xor_1_out & {8{xor_and_prime}};  // AND_Gate and_1, 8 bits wide
  assign and_2_out = op1 & op2;  // AND_Gate and_2, 8 bits wide
  assign and_3_out = op1 & {8{or_and_prime}};  // AND_Gate and_3, 8 bits wide
  assign and_4_out = op2 & {8{or_and_prime}};  // AND_Gate and_4, 8 bits wide
  assign or_1_out = and_2_out | and_3_out | and_4_out;  // OR_Gate or_1, 8 bits wide
  assign and_5_out = or_1_out & {8{not_1_out[7]}};  // AND_Gate and_5, 8 bits wide
  assign result = and_5_out | and_1_out;  // OR_Gate or_2, 8 bits wide
endmodule

module IR (
  input  [7:0] \input ,
  input  latch,
  input  \int ,
  input  Cl,
  input  Reset,
  output [7:0] Output
);

  wire [7:0] mux2x1_1_out;

  mux2x1 mux2x1_1 (.in0(\input ), .select(\int ), .in1(8'hd8), .out(mux2x1_1_out));
  Register #(.trigger("falling")) register_1 (.D(mux2x1_1_out), .en(latch), .Q(Output), .clk(Cl), .clr(Reset));

  // Notes on the sheet:
  //   input: pull=down
  //   interrupt instr. op-code
endmodule

module PS (
  input  ldPS,
  input  [3:0] CVZN,
  input  [7:0] bus_in,
  input  latch_CVZN,
  input  \assert ,
  input  Cl,
  input  Rset,
  output [7:0] bus_out,
  output [7:0] Output
);

  wire or_1_out;
  wire [3:0] controlled_buffer_1_out, controlled_buffer_2_out;

  assign controlled_buffer_1_out = latch_CVZN ? CVZN : 4'bz;  // Controlled_Buffer controlled_buffer_1
  or or_1 (or_1_out, latch_CVZN, ldPS);
  Register #(.width(4), .trigger("falling")) register_1 (
    .D(controlled_buffer_1_out), .en(or_1_out), .Q(Output[3:0]), .clk(Cl), .clr(Rset));
  Register #(.width(4), .trigger("falling")) register_2 (
    .D(controlled_buffer_2_out), .en(ldPS), .Q(Output[7:4]), .clk(Cl), .clr(Rset));
  assign {controlled_buffer_2_out, controlled_buffer_1_out} = ldPS ? bus_in : 8'bz;  // Controlled_Buffer controlled_buffer_2
  assign bus_out = \assert  ? Output : 8'bz;  // Controlled_Buffer controlled_buffer_3

  // Notes on the sheet:
  //   CVZN: pull=down
  //   latch_CVZN: pull=down
endmodule

// 3S&
module _4driver (
  input  in_1,
  input  in_2,
  output out_3,
  output out_4,
  output out_5,
  output out_6
);

  and and_1 (out_3, in_2, in_1);
  and and_2 (out_4, in_2, in_1);
  and and_3 (out_6, in_2, in_1);
  and and_4 (out_5, in_2, in_1);

  // Notes on the sheet:
  //   and_1 drives only 1 and floats otherwise
  //   and_2 drives only 1 and floats otherwise
  //   and_3 drives only 1 and floats otherwise
  //   and_4 drives only 1 and floats otherwise
endmodule

// 3S&
module _2driver (
  input  in_1,
  input  in_2,
  output out_3,
  output out_4
);

  and and_1 (out_3, in_2, in_1);
  and and_2 (out_4, in_2, in_1);

  // Notes on the sheet:
  //   and_1 drives only 1 and floats otherwise
  //   and_2 drives only 1 and floats otherwise
endmodule

// 3S&
module _6driver (
  input  in_1,
  input  in_2,
  output out_3,
  output out_4,
  output out_5,
  output out_6,
  output out_7,
  output out_8
);

  and and_1 (out_3, in_2, in_1);
  and and_2 (out_4, in_2, in_1);
  and and_3 (out_6, in_2, in_1);
  and and_4 (out_5, in_2, in_1);
  and and_5 (out_7, in_2, in_1);
  and and_6 (out_8, in_2, in_1);

  // Notes on the sheet:
  //   and_1 drives only 1 and floats otherwise
  //   and_2 drives only 1 and floats otherwise
  //   and_3 drives only 1 and floats otherwise
  //   and_4 drives only 1 and floats otherwise
  //   and_5 drives only 1 and floats otherwise
  //   and_6 drives only 1 and floats otherwise
endmodule

// 3S&
module _8driver (
  input  in_1,
  input  in_2,
  output out_3,
  output out_4,
  output out_5,
  output out_6,
  output out_7,
  output out_8,
  output out_9,
  output out_10
);

  and and_1 (out_3, in_2, in_1);
  and and_2 (out_4, in_2, in_1);
  and and_3 (out_6, in_2, in_1);
  and and_4 (out_5, in_2, in_1);
  and and_5 (out_7, in_2, in_1);
  and and_6 (out_9, in_2, in_1);
  and and_7 (out_8, in_2, in_1);
  and and_8 (out_10, in_2, in_1);

  // Notes on the sheet:
  //   and_1 drives only 1 and floats otherwise
  //   and_2 drives only 1 and floats otherwise
  //   and_3 drives only 1 and floats otherwise
  //   and_4 drives only 1 and floats otherwise
  //   and_5 drives only 1 and floats otherwise
  //   and_6 drives only 1 and floats otherwise
  //   and_7 drives only 1 and floats otherwise
  //   and_8 drives only 1 and floats otherwise
endmodule

module br_dcsn (
  input  [3:0] cccc,
  input  [3:0] CVZN,
  output go
);

  wire and_1_out, and_2_out, and_3_out, and_4_out, and_5_out, and_6_out, and_7_out, not_1_out, not_2_out,
       or_1_out, xnor_1_out;
  wire [3:0] decoder_2x4_1_out, decoder_2x4_2_out;

  not not_1 (not_1_out, cccc[3]);
  decoder_2x4 decoder_2x4_1 (.in(cccc[2:1]), .en(not_1_out), .out(decoder_2x4_1_out));
  decoder_2x4 decoder_2x4_2 (.in(cccc[2:1]), .en(cccc[3]), .out(decoder_2x4_2_out));
  and and_1 (and_1_out, decoder_2x4_1_out[0], CVZN[1]);
  and and_2 (and_2_out, decoder_2x4_1_out[1], CVZN[3]);
  and and_3 (and_3_out, decoder_2x4_1_out[2], CVZN[0]);
  and and_4 (and_4_out, decoder_2x4_1_out[3], CVZN[2]);
  not not_2 (not_2_out, CVZN[1]);
  xnor xnor_1 (xnor_1_out, CVZN[0], CVZN[2]);
  and and_5 (and_5_out, decoder_2x4_2_out[0], not_2_out, CVZN[3]);
  and and_6 (and_6_out, xnor_1_out, decoder_2x4_2_out[1]);
  and and_7 (and_7_out, not_2_out, xnor_1_out, decoder_2x4_2_out[2]);
  or or_1 (or_1_out, and_1_out, and_2_out, and_3_out, and_4_out, and_5_out, and_6_out, and_7_out, decoder_2x4_2_out[3]);
  xor xor_1 (go, cccc[0], or_1_out);

  // Notes on the sheet:
  //   N
  //   Z
  //   V
  //   C
  //   EQ
  //   HS/CS
  //   MI
  //   VS
  //   N=V
  //   Z'
  //   HI
  //   GE
  //   GT
  //   <always>
endmodule

// RS
module RS_latch (
  input  S,
  input  R,
  input  reset,
  output Q,
  output Q_prime
);

  S_R_Flip_Flop #(.trigger("high")) s_r_ff_1 (
    .S(S), .clk(1'b1), .R(R), .Q(Q), .Qn(Q_prime), .reset(reset));  // open: preset, en
endmodule

// I-arbiter
module simple_IA (
  input  IRQin,
  input  ACKin,
  input  rset,
  input  [2:0] vec,
  input  req,
  output [2:0] vecbus,
  output IRQout,
  output ACKout,
  output ack
);

  wire and_3_out, and_4_out, and_5_out, and_6_out, decoder_1_out0, decoder_1_out1, not_1_out, not_2_out,
       not_3_out, not_4_out, or_1_out;
  wire [1:0] and_1_out, register_1_q;

  and and_1 (and_1_out[0], ~register_1_q[0], ~register_1_q[1]);  // AND_Gate
  and and_2 (and_1_out[1], register_1_q[0], ~register_1_q[1]);  // AND_Gate
  Register #(.width(2)) register_1 (.D(and_1_out), .Q(register_1_q), .clk(or_1_out), .clr(rset));  // open: en
  or or_1 (or_1_out, and_3_out, and_4_out, and_6_out);
  Decoder #(.select(2), .disabled(0), .enable("false")) decoder_1 (
    .out0(decoder_1_out0), .out1(decoder_1_out1), .out2(ack), .sel(register_1_q));  // open: out3
  and and_3 (and_3_out, ack, not_1_out);
  not not_1 (not_1_out, ACKin);
  assign vecbus = ack ? vec : 3'bz;  // Controlled_Buffer controlled_buffer_1
  or or_2 (IRQout, and_5_out, not_2_out);
  not not_2 (not_2_out, not_3_out);
  not not_3 (not_3_out, decoder_1_out1);
  and and_4 (and_4_out, decoder_1_out1, ACKin);
  and and_5 (and_5_out, IRQin, decoder_1_out0);
  and and_6 (and_6_out, decoder_1_out0, req, not_4_out);
  not not_4 (not_4_out, ACKin);
  and and_7 (ACKout, decoder_1_out0, ACKin);
endmodule

// Arbiter
module IA (
  input  IRQ,
  input  Rset,
  input  IAck,
  input  [2:0] vec,
  input  IRQ_2,
  output [2:0] vecbus,
  output IRQ_3,
  output IAck_2,
  output IAck_3
);

  wire and_4_out, decoder_1_out0, decoder_1_out1, FE_out, not_1_out, not_2_out, not_3_out, not_4_out,
       not_5_out, not_6_out, not_7_out, or_1_out, or_2_out, or_3_out, RE_out, rs_latch_1_q_prime, S0_out,
       S1_out, S2_out;
  wire [1:0] and_1_out, register_1_q;

  and and_1 (and_1_out[0], ~register_1_q[0], ~register_1_q[1]);  // AND_Gate
  and and_2 (and_1_out[1], register_1_q[0], ~register_1_q[1]);  // AND_Gate
  and and_3 (IRQ_3, or_2_out, ~not_2_out);  // AND_Gate
  Register #(.width(2)) register_1 (.D(and_1_out), .Q(register_1_q), .clk(or_1_out), .clr(Rset));  // open: en
  not not_1 (not_1_out, IAck_3);
  not not_2 (not_2_out, not_1_out);
  Decoder #(.select(2), .disabled(0), .enable("false")) decoder_1 (
    .out0(decoder_1_out0), .out1(decoder_1_out1), .out2(IAck_3), .sel(register_1_q));  // open: out3
  assign vecbus = IAck_3 ? vec : 3'bz;  // Controlled_Buffer controlled_buffer_1
  or or_1 (or_1_out, S2_out, S1_out, S0_out);
  or or_2 (or_2_out, and_4_out, decoder_1_out1);
  and S2 (S2_out, IAck_3, ~IAck);  // AND_Gate
  and and_4 (and_4_out, IRQ, not_3_out);
  and S1 (S1_out, decoder_1_out1, IAck);
  and S0 (S0_out, decoder_1_out0, rs_latch_1_q_prime, not_5_out);
  not not_3 (not_3_out, not_4_out);
  not not_4 (not_4_out, decoder_1_out0);
  not not_5 (not_5_out, not_6_out);
  not not_6 (not_6_out, IRQ_2);
  not not_7 (not_7_out, IAck);
  and RE (RE_out, ~IRQ_2, IAck, not_7_out);  // AND_Gate
  or or_3 (or_3_out, Rset, FE_out);
  nor FE (FE_out, not_7_out, IAck);
  RS_latch rs_latch_1 (.S(RE_out), .R(or_3_out), .Q(IAck_2), .Q_prime(rs_latch_1_q_prime));  // open: reset

  // Notes on the sheet:
  //   idle
  //   disable
  //   IAck
endmodule

module iterator (
  input  dec_inc_prime,
  input  enable,
  input  Cl,
  input  reset,
  output [1:0] Rd
);

  wire [1:0] not_1_out, register_1_q;

  Register #(.width(2), .trigger("falling")) register_1 (
    .D(not_1_out), .en(enable), .Q(register_1_q), .clk(Cl), .clr(reset));
  not not_1 (not_1_out[0], register_1_q[0]);
  xor xor_1 (not_1_out[1], register_1_q[0], register_1_q[1]);
  assign Rd = {2{dec_inc_prime}} ^ register_1_q;  // XOR_Gate xor_2, 2 bits wide

  // Notes on the sheet:
  //   +1
endmodule

module check_cell (
  input  [1:0] in_1,
  input  [1:0] in_2,
  input  [1:0] in_3,
  output [1:0] out_4
);

  wire and_1_out, comparator_1_eq, comparator_2_eq;

  Comparator #(.width(2)) comparator_1 (.a(in_1), .b(in_2), .eq(comparator_1_eq));  // open: gt, lt
  Comparator #(.width(2)) comparator_2 (.a(in_2), .b(in_3), .eq(comparator_2_eq));  // open: gt, lt
  and and_1 (and_1_out, comparator_1_eq, comparator_2_eq);
  Multiplexer #(.width(2), .enable("false")) multiplexer_1 (.in0(2'b00), .in1(in_1), .out(out_4), .sel(and_1_out));
endmodule

// check_state
module check_all (
  input  [1:0] _0_0,
  input  [1:0] _0_1,
  input  [1:0] _0_2,
  input  [1:0] _1_0,
  input  [1:0] _1_1,
  input  [1:0] _1_2,
  input  [1:0] _2_0,
  input  [1:0] _2_1,
  input  [1:0] _2_2,
  output [1:0] out_10
);

  wire and_1_out, nor_1_out, nor_2_out, nor_3_out, nor_4_out, nor_5_out, nor_6_out, nor_7_out, nor_8_out,
       nor_9_out, or_1_out;
  wire [1:0] check_cell_1_out_4, check_cell_2_out_4, check_cell_3_out_4, check_cell_4_out_4,
       check_cell_5_out_4, check_cell_6_out_4, check_cell_7_out_4, check_cell_8_out_4, or_2_out;

  nor nor_1 (nor_1_out, _0_0[0], _0_0[1]);
  nor nor_2 (nor_2_out, _0_1[0], _0_1[1]);
  nor nor_3 (nor_3_out, _0_2[0], _0_2[1]);
  nor nor_4 (nor_4_out, _1_0[0], _1_0[1]);
  nor nor_5 (nor_5_out, _1_1[0], _1_1[1]);
  nor nor_6 (nor_6_out, _1_2[0], _1_2[1]);
  nor nor_7 (nor_7_out, _2_0[0], _2_0[1]);
  nor nor_8 (nor_8_out, _2_1[0], _2_1[1]);
  nor nor_9 (nor_9_out, _2_2[0], _2_2[1]);
  check_cell check_cell_1 (.in_1(_0_0), .in_2(_0_1), .in_3(_0_2), .out_4(check_cell_1_out_4));
  check_cell check_cell_2 (.in_1(_1_0), .in_2(_1_1), .in_3(_1_2), .out_4(check_cell_2_out_4));
  check_cell check_cell_3 (.in_1(_2_0), .in_2(_2_1), .in_3(_2_2), .out_4(check_cell_3_out_4));
  check_cell check_cell_4 (.in_1(_0_0), .in_2(_1_0), .in_3(_2_0), .out_4(check_cell_4_out_4));
  check_cell check_cell_5 (.in_1(_0_1), .in_2(_1_1), .in_3(_2_1), .out_4(check_cell_5_out_4));
  check_cell check_cell_6 (.in_1(_0_2), .in_2(_1_2), .in_3(_2_2), .out_4(check_cell_6_out_4));
  check_cell check_cell_7 (.in_1(_0_0), .in_2(_1_1), .in_3(_2_2), .out_4(check_cell_7_out_4));
  check_cell check_cell_8 (.in_1(_2_0), .in_2(_1_1), .in_3(_0_2), .out_4(check_cell_8_out_4));
  or or_1 (or_1_out, nor_1_out, nor_2_out, nor_3_out, nor_4_out, nor_5_out, nor_6_out, nor_7_out, nor_8_out, nor_9_out);
  assign or_2_out = check_cell_1_out_4 | check_cell_2_out_4 | check_cell_3_out_4 | check_cell_4_out_4 | check_cell_5_out_4 | check_cell_6_out_4 | check_cell_7_out_4 | check_cell_8_out_4;  // OR_Gate or_2, 2 bits wide
  and and_1 (and_1_out, ~or_2_out[0], ~or_2_out[1], ~or_1_out);  // AND_Gate
  Multiplexer #(.width(2), .enable("false")) multiplexer_1 (.in0(or_2_out), .in1(2'b11), .out(out_10), .sel(and_1_out));

  // Other names for the same wires on the sheet: _00[1:0] = _0_0; _01[1:0] = _0_1; _02[1:0] = _0_2; _10[1:0] = _1_0;
  //   _11[1:0] = _1_1; _12[1:0] = _1_2; _20[1:0] = _2_0; _21[1:0] = _2_1; _22[1:0] = _2_2
endmodule

module check_3cells (
  input  [1:0] ctrl,
  input  [1:0] val1,
  input  [3:0] addr1,
  input  [1:0] val2,
  input  [3:0] addr2,
  input  [1:0] val3,
  input  [3:0] addr3,
  output [3:0] out,
  output empty
);

  wire and_1_out, and_2_out, and_3_out, cmp_1_out_4, cmp_2_out_4, cmp_3_out_4, is_zero_1_out_2,
       is_zero_2_out_2, is_zero_3_out_2;
  wire [3:0] multiplexer_1_out, multiplexer_2_out;

  cmp cmp_1 (.in_1(ctrl), .in_2(val1), .in_3(val2), .out_4(cmp_1_out_4));
  and and_1 (and_1_out, cmp_1_out_4, is_zero_1_out_2);
  is_zero is_zero_1 (.in_1(val3), .out_2(is_zero_1_out_2));
  Multiplexer #(.width(4), .enable("false")) multiplexer_1 (
    .in0(4'b1111), .in1(addr3), .out(multiplexer_1_out), .sel(and_1_out));
  cmp cmp_2 (.in_1(ctrl), .in_2(val2), .in_3(val3), .out_4(cmp_2_out_4));
  is_zero is_zero_2 (.in_1(val1), .out_2(is_zero_2_out_2));
  and and_2 (and_2_out, cmp_2_out_4, is_zero_2_out_2);
  cmp cmp_3 (.in_1(ctrl), .in_2(val1), .in_3(val3), .out_4(cmp_3_out_4));
  is_zero is_zero_3 (.in_1(val2), .out_2(is_zero_3_out_2));
  Multiplexer #(.width(4), .enable("false")) multiplexer_2 (
    .in0(multiplexer_1_out), .in1(addr1), .out(multiplexer_2_out), .sel(and_2_out));
  and and_3 (and_3_out, cmp_3_out_4, is_zero_3_out_2);
  Multiplexer #(.width(4), .enable("false")) multiplexer_3 (
    .in0(multiplexer_2_out), .in1(addr2), .out(out), .sel(and_3_out));
  or or_1 (empty, and_3_out, and_2_out, and_1_out);

  // Other names for the same wires on the sheet: control[1:0] = ctrl
endmodule

module cmp (
  input  [1:0] in_1,
  input  [1:0] in_2,
  input  [1:0] in_3,
  output out_4
);

  wire comparator_1_eq, comparator_2_eq;

  Comparator #(.width(2)) comparator_1 (.a(in_1), .b(in_2), .eq(comparator_1_eq));  // open: gt, lt
  Comparator #(.width(2)) comparator_2 (.a(in_2), .b(in_3), .eq(comparator_2_eq));  // open: gt, lt
  and and_1 (out_4, comparator_1_eq, comparator_2_eq);
endmodule

module is_zero (
  input  [1:0] in_1,
  output out_2
);

  nor nor_1 (out_2, in_1[0], in_1[1]);
endmodule

module search_cell_cross (
  input  [1:0] _0_0,
  input  [1:0] _0_1,
  input  [1:0] _0_2,
  input  [1:0] _1_0,
  input  [1:0] _1_1,
  input  [1:0] _1_2,
  input  [1:0] _2_0,
  input  [1:0] _2_1,
  input  [1:0] _2_2,
  output [3:0] out_10
);

  wire check_3cells_1_empty, check_3cells_2_empty, check_3cells_3_empty, check_3cells_4_empty,
       check_3cells_5_empty, check_3cells_6_empty, check_3cells_7_empty, check_3cells_8_empty;
  wire [3:0] check_3cells_1_out, check_3cells_2_out, check_3cells_3_out, check_3cells_4_out,
       check_3cells_5_out, check_3cells_6_out, check_3cells_7_out, check_3cells_8_out, multiplexer_1_out,
       multiplexer_2_out, multiplexer_3_out, multiplexer_4_out, multiplexer_5_out, multiplexer_6_out,
       multiplexer_7_out;

  check_3cells check_3cells_1 (
    .ctrl(2'b10), .val1(_0_0), .addr1(4'b0000), .val2(_0_1), .addr2(4'b0001), .val3(_0_2), .addr3(4'b0010),
    .out(check_3cells_1_out), .empty(check_3cells_1_empty));
  Multiplexer #(.width(4), .enable("false")) multiplexer_1 (
    .in0(4'b1111), .in1(check_3cells_1_out), .out(multiplexer_1_out), .sel(check_3cells_1_empty));
  check_3cells check_3cells_2 (
    .ctrl(2'b10), .val1(_1_0), .addr1(4'b0100), .val2(_1_1), .addr2(4'b0101), .val3(_1_2), .addr3(4'b0110),
    .out(check_3cells_2_out), .empty(check_3cells_2_empty));
  check_3cells check_3cells_3 (
    .ctrl(2'b10), .val1(_2_0), .addr1(4'b1000), .val2(_2_1), .addr2(4'b1001), .val3(_2_2), .addr3(4'b1010),
    .out(check_3cells_3_out), .empty(check_3cells_3_empty));
  Multiplexer #(.width(4), .enable("false")) multiplexer_2 (
    .in0(multiplexer_1_out), .in1(check_3cells_2_out), .out(multiplexer_2_out), .sel(check_3cells_2_empty));
  Multiplexer #(.width(4), .enable("false")) multiplexer_3 (
    .in0(multiplexer_2_out), .in1(check_3cells_3_out), .out(multiplexer_3_out), .sel(check_3cells_3_empty));
  check_3cells check_3cells_4 (
    .ctrl(2'b10), .val1(_0_0), .addr1(4'b0000), .val2(_1_0), .addr2(4'b0100), .val3(_2_0), .addr3(4'b1000),
    .out(check_3cells_4_out), .empty(check_3cells_4_empty));
  Multiplexer #(.width(4), .enable("false")) multiplexer_4 (
    .in0(multiplexer_3_out), .in1(check_3cells_4_out), .out(multiplexer_4_out), .sel(check_3cells_4_empty));
  check_3cells check_3cells_5 (
    .ctrl(2'b10), .val1(_0_1), .addr1(4'b0001), .val2(_1_1), .addr2(4'b0101), .val3(_2_1), .addr3(4'b1001),
    .out(check_3cells_5_out), .empty(check_3cells_5_empty));
  Multiplexer #(.width(4), .enable("false")) multiplexer_5 (
    .in0(multiplexer_4_out), .in1(check_3cells_5_out), .out(multiplexer_5_out), .sel(check_3cells_5_empty));
  check_3cells check_3cells_6 (
    .ctrl(2'b10), .val1(_0_2), .addr1(4'b0010), .val2(_1_2), .addr2(4'b0110), .val3(_2_2), .addr3(4'b1010),
    .out(check_3cells_6_out), .empty(check_3cells_6_empty));
  check_3cells check_3cells_7 (
    .ctrl(2'b10), .val1(_0_0), .addr1(4'b0000), .val2(_1_1), .addr2(4'b0101), .val3(_2_2), .addr3(4'b1010),
    .out(check_3cells_7_out), .empty(check_3cells_7_empty));
  Multiplexer #(.width(4), .enable("false")) multiplexer_6 (
    .in0(multiplexer_5_out), .in1(check_3cells_6_out), .out(multiplexer_6_out), .sel(check_3cells_6_empty));
  check_3cells check_3cells_8 (
    .ctrl(2'b10), .val1(_0_2), .addr1(4'b0010), .val2(_1_1), .addr2(4'b0101), .val3(_2_0), .addr3(4'b1000),
    .out(check_3cells_8_out), .empty(check_3cells_8_empty));
  Multiplexer #(.width(4), .enable("false")) multiplexer_7 (
    .in0(multiplexer_6_out), .in1(check_3cells_7_out), .out(multiplexer_7_out), .sel(check_3cells_7_empty));
  Multiplexer #(.width(4), .enable("false")) multiplexer_8 (
    .in0(multiplexer_7_out), .in1(check_3cells_8_out), .out(out_10), .sel(check_3cells_8_empty));

  // Other names for the same wires on the sheet: _00[1:0] = _0_0; _01[1:0] = _0_1; _02[1:0] = _0_2; _10[1:0] = _1_0;
  //   _11[1:0] = _1_1; _12[1:0] = _1_2; _20[1:0] = _2_0; _21[1:0] = _2_1; _22[1:0] = _2_2
endmodule

module search_cell_nought (
  input  [1:0] _0_0,
  input  [1:0] _0_1,
  input  [1:0] _0_2,
  input  [1:0] _1_0,
  input  [1:0] _1_1,
  input  [1:0] _1_2,
  input  [1:0] _2_0,
  input  [1:0] _2_1,
  input  [1:0] _2_2,
  output [3:0] out_10
);

  wire check_3cells_1_empty, check_3cells_2_empty, check_3cells_3_empty, check_3cells_4_empty,
       check_3cells_5_empty, check_3cells_6_empty, check_3cells_7_empty, check_3cells_8_empty;
  wire [3:0] check_3cells_1_out, check_3cells_2_out, check_3cells_3_out, check_3cells_4_out,
       check_3cells_5_out, check_3cells_6_out, check_3cells_7_out, check_3cells_8_out, multiplexer_1_out,
       multiplexer_2_out, multiplexer_3_out, multiplexer_4_out, multiplexer_5_out, multiplexer_6_out,
       multiplexer_7_out;

  check_3cells check_3cells_1 (
    .ctrl(2'b01), .val1(_0_0), .addr1(4'b0000), .val2(_0_1), .addr2(4'b0001), .val3(_0_2), .addr3(4'b0010),
    .out(check_3cells_1_out), .empty(check_3cells_1_empty));
  Multiplexer #(.width(4), .enable("false")) multiplexer_1 (
    .in0(4'b1111), .in1(check_3cells_1_out), .out(multiplexer_1_out), .sel(check_3cells_1_empty));
  check_3cells check_3cells_2 (
    .ctrl(2'b01), .val1(_1_0), .addr1(4'b0100), .val2(_1_1), .addr2(4'b0101), .val3(_1_2), .addr3(4'b0110),
    .out(check_3cells_2_out), .empty(check_3cells_2_empty));
  check_3cells check_3cells_3 (
    .ctrl(2'b01), .val1(_2_0), .addr1(4'b1000), .val2(_2_1), .addr2(4'b1001), .val3(_2_2), .addr3(4'b1010),
    .out(check_3cells_3_out), .empty(check_3cells_3_empty));
  Multiplexer #(.width(4), .enable("false")) multiplexer_2 (
    .in0(multiplexer_1_out), .in1(check_3cells_2_out), .out(multiplexer_2_out), .sel(check_3cells_2_empty));
  Multiplexer #(.width(4), .enable("false")) multiplexer_3 (
    .in0(multiplexer_2_out), .in1(check_3cells_3_out), .out(multiplexer_3_out), .sel(check_3cells_3_empty));
  check_3cells check_3cells_4 (
    .ctrl(2'b01), .val1(_0_0), .addr1(4'b0000), .val2(_1_0), .addr2(4'b0100), .val3(_2_0), .addr3(4'b1000),
    .out(check_3cells_4_out), .empty(check_3cells_4_empty));
  Multiplexer #(.width(4), .enable("false")) multiplexer_4 (
    .in0(multiplexer_3_out), .in1(check_3cells_4_out), .out(multiplexer_4_out), .sel(check_3cells_4_empty));
  check_3cells check_3cells_5 (
    .ctrl(2'b01), .val1(_0_1), .addr1(4'b0001), .val2(_1_1), .addr2(4'b0101), .val3(_2_1), .addr3(4'b1001),
    .out(check_3cells_5_out), .empty(check_3cells_5_empty));
  Multiplexer #(.width(4), .enable("false")) multiplexer_5 (
    .in0(multiplexer_4_out), .in1(check_3cells_5_out), .out(multiplexer_5_out), .sel(check_3cells_5_empty));
  check_3cells check_3cells_6 (
    .ctrl(2'b01), .val1(_0_2), .addr1(4'b0010), .val2(_1_2), .addr2(4'b0110), .val3(_2_2), .addr3(4'b1010),
    .out(check_3cells_6_out), .empty(check_3cells_6_empty));
  check_3cells check_3cells_7 (
    .ctrl(2'b01), .val1(_0_0), .addr1(4'b0000), .val2(_1_1), .addr2(4'b0101), .val3(_2_2), .addr3(4'b1010),
    .out(check_3cells_7_out), .empty(check_3cells_7_empty));
  Multiplexer #(.width(4), .enable("false")) multiplexer_6 (
    .in0(multiplexer_5_out), .in1(check_3cells_6_out), .out(multiplexer_6_out), .sel(check_3cells_6_empty));
  check_3cells check_3cells_8 (
    .ctrl(2'b01), .val1(_0_2), .addr1(4'b0010), .val2(_1_1), .addr2(4'b0101), .val3(_2_0), .addr3(4'b1000),
    .out(check_3cells_8_out), .empty(check_3cells_8_empty));
  Multiplexer #(.width(4), .enable("false")) multiplexer_7 (
    .in0(multiplexer_6_out), .in1(check_3cells_7_out), .out(multiplexer_7_out), .sel(check_3cells_7_empty));
  Multiplexer #(.width(4), .enable("false")) multiplexer_8 (
    .in0(multiplexer_7_out), .in1(check_3cells_8_out), .out(out_10), .sel(check_3cells_8_empty));

  // Other names for the same wires on the sheet: _00[1:0] = _0_0; _01[1:0] = _0_1; _02[1:0] = _0_2; _10[1:0] = _1_0;
  //   _11[1:0] = _1_1; _12[1:0] = _1_2; _20[1:0] = _2_0; _21[1:0] = _2_1; _22[1:0] = _2_2
endmodule

module computer_turn (
  input  [1:0] _1,
  input  [1:0] _2,
  input  [1:0] _3,
  input  [1:0] _4,
  input  [1:0] _5,
  input  [1:0] _6,
  input  [1:0] _7,
  input  [1:0] _8,
  input  [1:0] _9,
  output [7:0] coords
);

  wire comparator_1_eq, comparator_2_eq;
  wire [3:0] cross_out_10, multiplexer_1_out, nought_out_10, rand_1_out_10;

  search_cell_cross \cross  (
    ._0_0(_1), ._0_1(_2), ._0_2(_3), ._1_0(_4), ._1_1(_5), ._1_2(_6), ._2_0(_7), ._2_1(_8), ._2_2(_9),
    .out_10(cross_out_10));
  \rand  rand_1 (
    ._1(_1), ._2(_2), ._3(_3), ._4(_4), ._5(_5), ._6(_6), ._7(_7), ._8(_8), ._9(_9), .out_10(rand_1_out_10));
  search_cell_nought nought (
    ._0_0(_1), ._0_1(_2), ._0_2(_3), ._1_0(_4), ._1_1(_5), ._1_2(_6), ._2_0(_7), ._2_1(_8), ._2_2(_9),
    .out_10(nought_out_10));
  Comparator #(.width(4)) comparator_1 (.a(cross_out_10), .b(4'b1111), .eq(comparator_1_eq));  // open: gt, lt
  Multiplexer #(.width(4), .enable("false")) multiplexer_1 (
    .in0(cross_out_10), .in1(rand_1_out_10), .out(multiplexer_1_out), .sel(comparator_1_eq));
  Comparator #(.width(4)) comparator_2 (.a(4'b1111), .b(nought_out_10), .eq(comparator_2_eq));  // open: gt, lt
  Multiplexer #(.width(4), .enable("false")) multiplexer_2 (
    .in0(nought_out_10), .in1(multiplexer_1_out), .out(coords[3:0]), .sel(comparator_2_eq));

  assign coords[7:4] = 4'b0000;
endmodule

module \rand  (
  input  [1:0] _1,
  input  [1:0] _2,
  input  [1:0] _3,
  input  [1:0] _4,
  input  [1:0] _5,
  input  [1:0] _6,
  input  [1:0] _7,
  input  [1:0] _8,
  input  [1:0] _9,
  output [3:0] out_10
);

  wire clock_1_out, clock_2_out, comparator_1_eq, nor_1_out;
  wire [1:0] multiplexer_1_out;
  wire [3:0] adder_1_out, counter_val_q, multiplexer_2_out;

  Clock clock_1 (.out(clock_1_out));
  Adder #(.width(4)) adder_1 (.a(counter_val_q), .b(4'b0001), .out(adder_1_out));  // open: cin, cout
  Register #(.width(4)) counter_val (
    .D(adder_1_out), .Q(counter_val_q), .clk(clock_1_out), .clr(comparator_1_eq));  // open: en
  Comparator #(.width(4)) comparator_1 (.a(counter_val_q), .b(4'b1010), .eq(comparator_1_eq));  // open: gt, lt
  Multiplexer #(.select(4), .width(2), .enable("false")) multiplexer_1 (
    .in0(_1), .in1(_2), .in2(_3), .in3(_4), .in4(_5), .in5(_6), .in6(_7), .in7(_8), .in8(_9), .in9(2'b01),
    .out(multiplexer_1_out), .sel(counter_val_q));  // open: in10, in11, in12, in13, in14, in15
  Multiplexer #(.select(4), .width(4), .enable("false")) multiplexer_2 (
    .in0(4'b0000), .in1(4'b0001), .in2(4'b0010), .in3(4'b0100), .in4(4'b0101), .in5(4'b0110), .in6(4'b1000),
    .in7(4'b1001), .in8(4'b1010), .in9(4'b0000), .out(multiplexer_2_out), .sel(counter_val_q));  // open: in10, in11, in12, in13, in14, in15
  // Probe on counter_val_q
  nor nor_1 (nor_1_out, multiplexer_1_out[0], multiplexer_1_out[1]);
  Register #(.width(4)) last_null (.D(multiplexer_2_out), .en(nor_1_out), .Q(out_10), .clk(clock_2_out));  // open: clr
  Clock clock_2 (.out(clock_2_out));
endmodule
